# Fritzing sketch GloveNode_schematic (saved by Fritzing 0.9.3b)

parts:
  U1 = XBee
  3-Axis_Accelerometer1 = 3-Axis Accelerometer Breakout - MMA8452Q
  U2 = LIPO-2000mAh [package=lipo-2000]
  Part1 = Arduino Nano (Rev3.0)

nets:
  VCC: U1.VCC, 3-Axis_Accelerometer1.3.3V, U2.+, Part1.VIN
  N1: U1.pin3, Part1.D0/RX
  N2: U1.pin4, Part1.D1/TX
  GND: U1.GND, 3-Axis_Accelerometer1.GND, U2.-
  N3: 3-Axis_Accelerometer1.SDA, Part1.A4
  N4: 3-Axis_Accelerometer1.SCL, Part1.A5
