# Fritzing sketch MotorDrive_schematic (saved by Fritzing 0.9.3b)

parts:
  Part1 = Arduino Mega 2560 (Rev3)
  HC-SR04_Sensor_1 = HC-SR04 Ultrasonic Distance Sensor
  HC-SR04_Sensor_2 = HC-SR04 Ultrasonic Distance Sensor
  HC-SR04_Sensor_3 = HC-SR04 Ultrasonic Distance Sensor
  HC-SR04_Sensor_4 = HC-SR04 Ultrasonic Distance Sensor
  M1 = DC Motor
  M2 = DC Motor
  U1 = XBee
  3-Axis_Accelerometer1 = 3-Axis Accelerometer Breakout - MMA8452Q
  Part2 = Adafruit Motor/Stepper/Servo Shield [part_number="Adafruit #1438"]

nets:
  N1: Part1.D21/SCL, 3-Axis_Accelerometer1.SCL
  N2: Part1.D20/SDA, 3-Axis_Accelerometer1.SDA
  N3: Part1.D15/RX3, U1.pin2, U1.pin3
  N4: Part1.D14/TX3, U1.pin4
  5V: Part1.5V, HC-SR04_Sensor_2.VCC
  N5: Part1.D35, HC-SR04_Sensor_1.TRIG
  N6: Part1.D37, HC-SR04_Sensor_1.ECHO
  N7: Part1.D39, HC-SR04_Sensor_3.TRIG
  N8: Part1.D41, HC-SR04_Sensor_3.ECHO
  N9: Part1.D43, HC-SR04_Sensor_2.TRIG
  N10: Part1.D45, HC-SR04_Sensor_2.ECHO
  N11: Part1.D47, HC-SR04_Sensor_4.TRIG
  N12: Part1.D49, HC-SR04_Sensor_4.ECHO
  GND: Part1.GND, HC-SR04_Sensor_2.GND
  N13: M1.pin_1, Part2.M1B
  N14: M1.pin_2, Part2.M1A
  N15: M2.pin_1, Part2.M2A
  N16: M2.pin_2, Part2.M2B
  3.3V: 3-Axis_Accelerometer1.3.3V, Part2.+3V3

custom parts:
  Adafruit Motor/Stepper/Servo Shield: The original Adafruit Motorshield kit is one of our most beloved kits, which is why we decided to make something even better. We have upgraded the shield kit to make the bestest, easiest way to drive DC and Stepper motors. This shield will make quick work of your next robotics project! We kept the ability to drive up to 4 DC motors or 2 stepper motors, but added many improvements: Instead of a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
