# Fritzing sketch RaspNode_schematic (saved by Fritzing 0.9.3b)

parts:
  Raspberry_Pi_1 = Raspberry Pi 3 [part_number=RPI-3-V1.2]
  J1 = Basic Servo
  SP1 = SPEAKER [package=pcb_mount_speaker]
  MIC1 = Microphone
  LED1 = RGB LED (com. anode, rbg) [package="5 mm [THT]"]
  LED2 = RGB LED (com. anode, rbg) [package="5 mm [THT]"]
  R1 = Resistor [tolerance=±5% resistance=220 package="2512 [SMD]"]
  R2 = Resistor [tolerance=±5% resistance=220 package="2512 [SMD]"]
  R3 = Resistor [tolerance=±5% resistance=220 package="2512 [SMD]"]
  R4 = Resistor [tolerance=±5% resistance=220 package="2512 [SMD]"]
  R5 = Resistor [tolerance=±5% resistance=220 package="2512 [SMD]"]
  R6 = Resistor [tolerance=±5% resistance=220 package="2512 [SMD]"]
  J2 = Basic Servo
  J3 = Basic Servo
  J4 = Basic Servo

nets:
  N1: Raspberry_Pi_1.3v3, J3.pulse
  GND: Raspberry_Pi_1.GND, SP1.+, MIC1.pin1, LED1.green_cathode, LED2.green_cathode, R1.Pin_1, J3.gnd
  N2: Raspberry_Pi_1.GIPO21, SP1.-
  N3: Raspberry_Pi_1.GIPO16, MIC1.pin2
  N4: Raspberry_Pi_1.GIPO12, J2.pulse
  N5: Raspberry_Pi_1.ID_SC, R6.Pin_1
  N6: Raspberry_Pi_1.GIPO7, R5.Pin_1
  N7: Raspberry_Pi_1.GIPO8, R4.Pin_1
  N8: Raspberry_Pi_1.GIPO25, J1.pulse
  N9: Raspberry_Pi_1.GIPO24, R3.Pin_1
  N10: Raspberry_Pi_1.GIPO23, R2.Pin_1
  N11: Raspberry_Pi_1.GIPO15, J4.pulse
  5V: Raspberry_Pi_1.5V, J3.vcc
